# Fritzing sketch Slot_Machine_MIDTERM (saved by Fritzing 1.0.4)
breadboards: 2

parts:
  A1 = Particle - Photon2
  DFRobot_DFPlayer_Mini1 = DFRobot DFPlayer Mini [part_number=DFR0299]
  SP1 = SPEAKER [package=pcb_mount_speaker]
  U1 = ENCODER_RGB [package=encoder_led_2]
  S1 = Round Pushbutton
  R1 = Resistor [tolerance=±5% resistance=220 package="0603 [SMD]"]
  OLED_I2C2 = OLED 128x64 I2C Monochrome Display

nets:
  VCC: A1.Pin_2, A1.Pin_31, DFRobot_DFPlayer_Mini1.VCC, U1.+, S1.leg1, R1.Pin_0, OLED_I2C2.VDD
  N1: A1.Pin_4, A1.Pin_30, DFRobot_DFPlayer_Mini1.GND-1, DFRobot_DFPlayer_Mini1.GND-2, OLED_I2C2.GND
  N2: A1.Pin_5, U1.R
  N3: A1.Pin_6, U1.G
  N4: A1.Pin_7, U1.B
  N5: A1.Pin_8, U1.SW
  N6: A1.Pin_14, DFRobot_DFPlayer_Mini1.TX
  N7: A1.Pin_15, DFRobot_DFPlayer_Mini1.RX
  N8: A1.Pin_17, OLED_I2C2.SDA
  N9: A1.Pin_18, OLED_I2C2.SCK
  N10: A1.Pin_19, S1.leg0, R1.Pin_1
  N11: DFRobot_DFPlayer_Mini1.SPK_1, SP1.-
  N12: DFRobot_DFPlayer_Mini1.SPK_2, SP1.+

custom parts:
  Particle - Photon2: The Photon 2 is a microcontroller and Wi-Fi networking developed by particle. Features: 802.11a/b/g/n Wi-Fi, 2.4 GHz and 5 GHz Integrated PCB antenna Integrated U.FL connector for external antenna Integrated RF switch BLE 5 using same antenna as Wi-Fi Realtek RTL8721DM MCU ARM Cortex M33 CPU, 200 MHz 2048 KB (2 MB) user application maximum size 3072 KB (3 MB) of RAM available to user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
  ENCODER_RGB: SparkFun RGB rotary Encoder
